// Logisim project Cell12.circ as structural Verilog: 1 circuit, main circuit main
module main (
  input  A,
  input  B,
  input  C,
  input  D,
  output Z
);

  nor nor_1 (Z, A, B, C, D);
endmodule
