// Logisim project Cell13b.circ as structural Verilog: 1 circuit, main circuit main
module main (
  input  A,
  input  B,
  output Z
);

  wire nand_1_out;

  nand nand_1 (nand_1_out, A, B);
  not not_1 (Z, nand_1_out);
endmodule
