// Logisim project Cell13c.circ as structural Verilog: 1 circuit, main circuit main
module main (
  input  A,
  output Z
);

  wire not_1_out;

  not not_1 (not_1_out, A);
  not not_2 (Z, not_1_out);
endmodule
