// Logisim project Cell13e.circ as structural Verilog: 1 circuit, main circuit main
module main (
  input  A,
  input  B,
  output Z
);

  wire nor_1_out, not_1_out;

  nor nor_1 (nor_1_out, A, B);
  not not_1 (not_1_out, nor_1_out);
  not not_2 (Z, not_1_out);
endmodule
