// Logisim project Cell13f.circ as structural Verilog: 2 circuits, main circuit main
module main (
  input  A,
  input  B,
  output Z
);

  wire nor_1_out;

  nor nor_1 (nor_1_out, A, B);
  not not_1 (Z, nor_1_out);
endmodule

module OR2 (
  input  a,
  input  b,
  output x
);

  wire nor_1_out;

  nor nor_1 (nor_1_out, a, b);
  not not_1 (x, nor_1_out);
endmodule
