// Logisim project Cell33b.circ as structural Verilog: 1 circuit, main circuit main
module main (
  input  A,
  input  B,
  input  C,
  output Z
);

  wire nand_1_out;

  nand nand_1 (nand_1_out, A, B, C);
  not not_1 (Z, nand_1_out);
endmodule
