// Logisim project Cell36b.circ as structural Verilog: 1 circuit, main circuit main
module main (
  input  A,
  input  B,
  input  C,
  input  D,
  input  E,
  input  F,
  input  G,
  input  H,
  output Z
);

  wire nand_1_out, nor_1_out, nor_2_out;

  nor nor_1 (nor_1_out, A, B, C, D);
  nor nor_2 (nor_2_out, E, F, G, H);
  nand nand_1 (nand_1_out, nor_1_out, nor_2_out);
  not not_1 (Z, nand_1_out);
endmodule
