// Logisim project Cell9.circ as structural Verilog: 1 circuit, main circuit main
module main (
  input  in_1,
  output out_2
);

  not not_1 (out_2, in_1);
  not not_2 (out_2, in_1);
endmodule
